# Fritzing sketch wiring (saved by Fritzing 0.9.3b)
breadboards: 1

parts:
  Teensy1 = Teensy 2.0
  Part1 = Adafruit MCP4725 Breakout Board - 12-Bit DAC [part_number="Adafruit #935"]
  IC1 = IC, DIP package, 8 pins [chip_label=UA741]
  IC2 = IC, DIP package, 8 pins [chip_label=7660s part_number=ICL7660S]
  C1 = Ceramic Capacitor [capacitance=10µF package="100 mil [THT, multilayer]"]
  C2 = Ceramic Capacitor [capacitance=10µF package="100 mil [THT, multilayer]"]
  R1 = Resistor [tolerance=±5% resistance=10k package=THT]
  R2 = Resistor [tolerance=±5% resistance=10k package=THT]
  U1 = BNC socket [package=bnc]
  U2 = BNC socket [package=bnc]

nets:
  GND: Teensy1.GND, Part1.GND, IC2.pin3, C2.1, U1.GND, U2.GND
  N1: Teensy1.D0, Part1.SCL
  N2: Teensy1.D1, Part1.SDA
  N3: Teensy1.D2, U1.OUT
  5V: Teensy1.VCC, Part1.VDD, IC1.pin7, IC2.pin8, R1.Pin_1
  N4: Part1.VOUT, IC1.pin3
  N5: IC1.pin2, R1.Pin_0, R2.Pin_0
  N6: IC1.pin4, IC2.pin5, C2.0
  N7: IC1.pin6, R2.Pin_1, U2.OUT
  N8: IC2.pin2, C1.0
  N9: IC2.pin4, C1.1

custom parts:
  Adafruit MCP4725 Breakout Board - 12-Bit DAC: Your microcontroller probably has an ADC (analog -> digital converter) but does it have a DAC (digital -> analog converter)??? Now it can! This breakout board features the easy-to-use MCP4725 12-bit DAC. Control it via I2C and send it the value you want it to output, and the VOUT pin will have it. Great for audio / analog projects, such as when you can't use PWM but need a sine wave or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
